# Fritzing sketch half_strip2 (saved by Fritzing 0.9.3b)
circuit board: 8.46667cm x 5.64444cm
stripboards: 1

parts:
  R1 = Resistor [tolerance=±5% resistance=1k package=THT]
  C1 = Ceramic Capacitor [capacitance=100nF package="100 mil [THT, multilayer]"]
  C2 = Ceramic Capacitor [capacitance=100nF package="100 mil [THT, multilayer]"]
  DIO_vref = female pin header, 1 pin [form="♀ (female)"]
  DIO_com = female pin header, 1 pin [form="♀ (female)"]
  POWER_gnd = female pin header, 1 pin [form="♀ (female)"]
  POWER_12v = female pin header, 1 pin [form="♀ (female)"]
  POWER_5v = female pin header, 1 pin [form="♀ (female)"]
  R2 = Resistor [tolerance=±5% resistance=1k package=THT]
  R3 = Resistor [tolerance=±5% resistance=10k package=THT]
  EXT_gnd = female pin header, 1 pin [form="♀ (female)"]
  DIO_ext = female pin header, 1 pin [form="♀ (female)"]
  Q1 = Basic FET N-Channel [package="TO220 [THT]"]
  R5 = Resistor [tolerance=±5% resistance=10k package=THT]
  DIO_bed = female pin header, 1 pin [form="♀ (female)"]
  Q2 = Basic FET N-Channel [package="TO220 [THT]"]
  BED_gnd = female pin header, 1 pin [form="♀ (female)"]
  EXT_term1 = female pin header, 1 pin [form="♀ (female)"]
  EXT_term2 = female pin header, 1 pin [form="♀ (female)"]
  C3 = Electrolytic Capacitor [capacitance=1µF package="100 mil [THT, electrolytic]"]
  R6 = Resistor [tolerance=±5% resistance=466 package=THT]
  DIO_extai = female pin header, 1 pin [form="♀ (female)"]
  C4 = Electrolytic Capacitor [capacitance=1µF package="100 mil [THT, electrolytic]"]
  R7 = Resistor [tolerance=±5% resistance=325 package=THT]
  BED_term1 = female pin header, 1 pin [form="♀ (female)"]
  BED_term2 = female pin header, 1 pin [form="♀ (female)"]
  DIO_bedai = female pin header, 1 pin [form="♀ (female)"]
  U1 = Voltage Regulator - 5V [package="TO220 [THT]"]
  BED_12 = female pin header, 1 pin [form="♀ (female)"]
  EXT_12 = female pin header, 1 pin [form="♀ (female)"]
  R4 = Resistor [tolerance=±5% resistance=1k package=THT]
  R8 = Resistor [tolerance=±5% resistance=1k package=THT]
  DIO_gnd1 = female pin header, 1 pin [form="♀ (female)"]

nets:
  5V: R1.Pin_0, C2.1, POWER_5v.pin1, EXT_term1.pin1, C4.+, BED_term1.pin1, U1.output_voltage
  N1: R1.Pin_1, DIO_vref.pin1
  GND: C1.0, C2.0, POWER_gnd.pin1, R3.Pin_1, Q1.source, R5.Pin_1, Q2.source, C3.-, R6.Pin_0, R7.Pin_0, U1.GND, R8.Pin_0, DIO_gnd1.pin1
  12V: C1.1, POWER_12v.pin1, U1.input_voltage, BED_12.pin1, EXT_12.pin1
  N2: DIO_com.pin1, R8.Pin_1
  N3: R2.Pin_0, DIO_ext.pin1
  N4: R2.Pin_1, R3.Pin_0, Q1.gate
  N5: EXT_gnd.pin1, Q1.drain
  N6: R5.Pin_0, Q2.gate, R4.Pin_1
  N7: DIO_bed.pin1, R4.Pin_0
  N8: Q2.drain, BED_gnd.pin1
  N9: EXT_term2.pin1, C3.+, R6.Pin_1, DIO_extai.pin1
  N10: C4.-, R7.Pin_1, BED_term2.pin1, DIO_bedai.pin1
